# Fritzing sketch Fotores (saved by Fritzing 0.9.3b)
breadboards: 1

parts:
  Componente1 = Arduino Uno (Rev3)
  R1 = Resistor [tolerance=±5% resistance=10k package=THT]
  R2 = Resistor [tolerance=±5% resistance=680 package=THT]
  R3 = Photocell (LDR) [package=THT]
  R4 = Resistor [tolerance=±5% resistance=330 package=THT]
  R5 = Resistor [tolerance=±5% resistance=330 package=THT]
  SPKR1 = Loudspeaker

nets:
  N1: Componente1.A5/SCL, R2.Pin_1, R3.pin_0
  N2: Componente1.D8, R4.Pin_0
  N3: Componente1.5V, R3.pin_1
  N4: Componente1.GND, R1.Pin_0, SPKR1.pin1
  N5: R1.Pin_1, R2.Pin_0
  N6: R4.Pin_1, R5.Pin_0
  N7: R5.Pin_1, SPKR1.pin2

// code stored in the sketch: main.ino
#include "pitches.h"

int analogInPin = A5;
int sensorValue = 0;

int times = 100;

// notes to play, corresponding to the 3 sensors:
int notes[] = {
  NOTE_A4, NOTE_B4, NOTE_C3, NOTE_D4, NOTE_E4, NOTE_F4, NOTE_G4
};

void setup() {
  Serial.begin(9600);
  pinMode( analogInPin, INPUT);
}

void loop() {
  sensorValue = analogRead(analogInPin);            

  Serial.print("sensor = " );
  Serial.println(sensorValue);
  Serial.print("times left =");
  Serial.println(times);
   playTone();     

times--;
if(times == 0)
exit(0);
  delay(1000);
}

void playTone()
{
  int step = 1001 / 6;
  for(int i = 0; i < 7; i++)
  {
    if(sensorValue < step * i)
    {
      tone(8, notes[i], 400);
      break;
    }
  }
}
